# Fritzing sketch h4f_reservoir_flusher (saved by Fritzing 0.8.7b)
circuit board: 8.46667cm x 5.64444cm
breadboards: 1

parts:
  Part1 = Arduino Uno (Rev3) - ICSP
  LDR = Photocell (LDR) [package=THT]
  R2 = Resistor [tolerance=±5% resistance=100k power=25mW package=THT]
  HC-SR04 = SRF05 Ultrasonic Rangefinder
  J1 = Basic Servo
  LED1 = LED - 5mm [color="Red (633nm)" package="5 mm [THT]"]
  LED2 = LED - 5mm [color="Green (570nm)" package="5 mm [THT]"]
  R3 = Resistor [tolerance=±5% resistance=470 power=25mW package=THT]
  R4 = Resistor [tolerance=±5% resistance=470 power=25mW package=THT]
  J3 = Power Jack [package=power_jack_pth_lock]

nets:
  5V: Part1.5V, LDR.pin_1, HC-SR04.VCC
  GND: Part1.GND, R2.Pin_0, HC-SR04.GND, J1.gnd, R3.Pin_0, R4.Pin_0, J3.GND
  N1: Part1.D9_PWM, J1.pulse
  N2: Part1.D10_PWM/SS, LED2.anode
  N3: Part1.D11_PWM/MOSI, LED1.anode
  N4: Part1.D2, LDR.pin_0, R2.Pin_1
  N5: Part1.D5_PWM, HC-SR04.Echo
  N6: Part1.D6_PWM, HC-SR04.Trig
  N7: J1.vcc, J3.PWR
  N8: LED1.cathode, R4.Pin_1
  N9: LED2.cathode, R3.Pin_1
